# Fritzing sketch PiFanControlFinal (saved by Fritzing 0.9.10b)
circuit board: 1.07823cm x 2.79996cm
breadboards: 1

parts:
  R1 = Resistor [tolerance=±5% power=0.25 resistance=100 package=THT]
  C1815 = NPN-Transistor [package="TO92 [THT]"]
  J2 = male pin header, 2 pins [form="♂ (male)"]
  J3 = Dagu DGServo 9g header connector (female) [package=THT]

nets:
  N1: R1.Pin_0, J3.GPIO14
  N2: R1.Pin_1, C1815.B
  N3: C1815.E, J3.Ground
  N4: C1815.C, J2.pin1
  N5: J2.pin2, J3.VCC(5V)

custom parts:
  Dagu DGServo 9g header connector (female): Dagu DGServo 9g header connector (female) This part represents the header plug found on the DGServo 9g. It is based on the standard female header, but is labelled to clearly indicate the ground, Vcc and pulse pins in schematic view. To use it, simply plug this part onto whichever header pins you are using, then attach the wires from a DGServo 9g part to the back of it. In schematic view,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
